# Fritzing sketch arduinoHookup (saved by Fritzing 0.9.3b)

parts:
  Part1 = Arduino Uno (Rev3)
  S1 = Pushbutton [package="[THT]"]
  R3 = Trimmer Potentiometer [maximum_resistance=10kΩ package=THT]
  R4 = Resistor [tolerance=±5% resistance=220 package=THT]
  OMRON1 = OMRON PCB Power Relay – G5LE [part_number="G5LE-1\n" package=THT]
  OMRON2 = OMRON PCB Power Relay – G5LE [part_number="G5LE-1\n" package=THT]
  L1 = Inductor [package="400 mil [THT]"]
  R2 = Resistor [tolerance=±5% resistance=10k package=THT]
  LED1 = smd LED [color="Red (633nm)" package="1206 [SMD]"]
  R1 = Resistor [tolerance=±5% resistance=220 package=THT]
  U2 = MAX6675 [package=so08]
  R5 = Temperature Sensor (Thermistor) [thermistor_type=NTC package=THT]
  U3 = MAX6675 [package=so08]
  R7 = Temperature Sensor (Thermistor) [thermistor_type=NTC package=THT]

nets:
  N1: Part1.A5/SCL, R4.Pin_1
  VDD: Part1.D8, U2.VDD, U3.VDD
  N2: Part1.D12/MISO, OMRON2.COIL1
  N3: Part1.D13/SCK, OMRON1.COIL1
  VSS: Part1.GND, R3.leg1, OMRON1.COIL2, OMRON2.COIL2, R2.Pin_0, R1.Pin_1, U2.VSS, U3.VSS
  N4: Part1.D2, LED1.anode
  N5: Part1.D3_PWM, S1.Pin_1, S1.Pin_2, R2.Pin_1
  N6: Part1.5V, R3.leg2
  N7: R3.wiper, R4.Pin_0
  N8: OMRON2.B, L1.pin_1
  N9: LED1.cathode, R1.Pin_0
  N10: U2.SCK, R5.pin_1
  N11: U2.CS, R5.pin_0
  N12: U3.SCK, R7.pin_1
  N13: U3.CS, R7.pin_0

notes:
  Toaster Oven
  Element A/C
  Circuit
  Zero-crossing optoisolated Solid State Relays
  Potentiometer may stand in for thermocouple / TC amplifier during testing
  Thermocouple Amplifier MAX31855 breakout board (1-wire)
